# Fritzing sketch TurtleFeeder (saved by Fritzing 0.9.3b)
circuit board: 6cm x 4cm
breadboards: 1

parts:
  D2F1 = D2F-FL Omron Snap Action Limit Switch with Level
  M1 = DC Motor
  J2 = Camdenboss CTB0158-4 [part_number=CTB0158-4 package=THT]
  H1 = polarizedheader 4pin 0.156in [package=THT]
  Q1 = NPN-Transistor [package="TO92 [THT]"]
  R1 = Resistor [tolerance=±5% resistance=220 package=THT]
  D1 = Rectifier Diode [part_number=1N4001 package="300 mil [THT]"]
  WeMos_D1_Mini1 = WeMos D1 Mini

nets:
  N1: D2F1.COM, J2.pin1
  N2: D2F1.NO, J2.pin2
  N3: M1.pin_1, J2.pin4
  N4: M1.pin_2, J2.pin3
  N5: H1.pin1, WeMos_D1_Mini1.D1
  N6: H1.pin2, Q1.E, WeMos_D1_Mini1.G
  N7: H1.pin3, Q1.C, D1.anode
  N8: H1.pin4, D1.cathode, WeMos_D1_Mini1.5V
  N9: Q1.B, R1.Pin_1
  N10: R1.Pin_0, WeMos_D1_Mini1.D2

custom parts:
  D2F-FL Omron Snap Action Limit Switch with Level: Snap action switch with stainless steel lever.
